# Fritzing sketch rover (saved by Fritzing 0.9.3b)
breadboards: 1

parts:
  Raspberry_Pi1 = Raspberry Pi 2
  M1 = DC Motor
  VCC1 = Battery
  J1 = Basic Servo
  IC1 = L293D [package=THT]
  C1 = Electrolytic Capacitor [capacitance=100µF voltage=25V package="100 mil [THT, electrolytic]"]
  R1 = Resistor [tolerance=±5% resistance=220 package=THT]

nets:
  N1: Raspberry_Pi1.GPIO4, IC1.Enable_1
  N2: Raspberry_Pi1.GPIO17, IC1.In_1
  N3: Raspberry_Pi1.GPIO10, R1.Pin_1
  N4: Raspberry_Pi1.GPIO18, IC1.In_2
  GND: Raspberry_Pi1.GND, VCC1.-, J1.gnd, IC1.Out_4_(_Controlled_by_Enable_2_), C1.-
  5V: Raspberry_Pi1.5V, J1.vcc, IC1.+V, C1.+
  N5: M1.pin_1, IC1.Out_1_(_Controlled_by_Enable_1_)
  N6: M1.pin_2, IC1.Out_2_(_Controlled_by_Enable_1_)
  N7: VCC1.+, IC1.+Vmotor
  N8: J1.pulse, R1.Pin_0

notes:
  The Raspberry Pi is powered by a 5V power bank
  6 AA batteries provide power to the DC motor through the driver
  DC motor for the forward and backward movement of the rover
  Powered by 6 AA batteries
  Servo motor (SM-S2309S) powered by the Raspberry Pi's GPIO.
  Uses Pin 19 (GPIO10) for the signal transmission
  (10th pin of the lower line)
  The outer line is + (5v) from the Raspberry Pi
  L293DNE motor driver
  Brown: Negative, Red: Positive, Yellow: Signal
